# Fritzing sketch Controller-Schematic-Rev_D (saved by Fritzing 0.9.10b)
breadboards: 4

parts:
  Part3 = Arduino Nano 33 IOT
  LED1 = LED - 5mm [color="Red (633nm)" current=0.030 package="5 mm [THT]"]
  LED2 = LED - 5mm [color="Red (633nm)" current=0.030 package="5 mm [THT]"]
  LED3 = LED - 5mm [color="Red (633nm)" current=0.030 package="5 mm [THT]"]
  LED4 = LED - 5mm [color="Red (633nm)" current=0.030 package="5 mm [THT]"]
  LED5 = LED - 5mm [color="Red (633nm)" current=0.030 package="5 mm [THT]"]
  LED6 = LED - 5mm [color="Red (633nm)" current=0.030 package="5 mm [THT]"]
  LED7 = LED - 5mm [color="Red (633nm)" current=0.030 package="5 mm [THT]"]
  LED8 = LED - 5mm [color="Red (633nm)" current=30mA package="5 mm [THT]"]
  R25 = Resistor [tolerance=±5% power=0.25 resistance=470 package=THT]
  R26 = Resistor [tolerance=±5% power=0.25 resistance=470 package=THT]
  R28 = Resistor [tolerance=±5% power=0.25 resistance=470 package=THT]
  R29 = Resistor [tolerance=±5% power=0.25 resistance=470 package=THT]
  R31 = Resistor [tolerance=±5% power=0.25 resistance=470 package=THT]
  R32 = Resistor [tolerance=±5% power=0.25 resistance=470 package=THT]
  LM1084-3_3V1 = Voltage Regulator - 3.3V [part_number=LM1084IT-3.3/NOPB package="TO220 [THT]"]
  C3 = Tantalum Capacitor [capacitance=10µF voltage=10V package="200 mil [THT, tantalum]"]
  C4 = Electrolytic Capacitor [capacitance=10µF voltage=16V part_number=ECA-1CM100I package="100 mil [THT, electrolytic]"]
  OX = DB9 Connector [package=db9]
  FUEL = DB9 Connector [package=db9]
  EXT = DB9 Connector [package=db9]
  R39 = Resistor [tolerance=±5% power=0.25 resistance=470 package=THT]
  R40 = Resistor [tolerance=±5% power=0.25 resistance=470 package=THT]
  FUEL_2 = IC, DIP package, 8 pins [chip_label=LTC1690]
  OX_2 = IC, DIP package, 8 pins [chip_label=LTC1690]
  EXT_2 = IC, DIP package, 8 pins [chip_label=LTC1690]
  STEP_UP = SSOP24 [chip_label=IC part_number=SN74AXC4T774-Q1 package=SSOP]
  STEP_DOWN = SSOP24 [chip_label=IC part_number=SN74AXC4T774-Q1 package=SSOP]
  RX_Enable = single row smd female pin header, 2 pins [form="♀ (female)"]
  TX_Enable = single row smd female pin header, 2 pins [form="♀ (female)"]
  74HCT595 = SO16 [chip_label=IC package=SO]  # not connected
  C3_2 = Electrolytic Capacitor [capacitance=1µF voltage=5V package="100 mil [THT, electrolytic]"]
  C5 = Electrolytic Capacitor [capacitance=0.1µF voltage=5V package="100 mil [THT, electrolytic]"]
  C6 = Electrolytic Capacitor [capacitance=1µF voltage=5V package="100 mil [THT, electrolytic]"]
  C7 = Electrolytic Capacitor [capacitance=0.1µF voltage=5V package="100 mil [THT, electrolytic]"]
  C8 = Electrolytic Capacitor [capacitance=1µF voltage=5V package="100 mil [THT, electrolytic]"]
  C9 = Electrolytic Capacitor [capacitance=1µF voltage=5V package="100 mil [THT, electrolytic]"]
  C10 = Electrolytic Capacitor [capacitance=1µF voltage=5V package="100 mil [THT, electrolytic]"]
  C11 = Electrolytic Capacitor [capacitance=1µF voltage=5V package="100 mil [THT, electrolytic]"]

nets:
  N1: Part3.RX, RX_Enable.pin2
  N2: Part3.TX, TX_Enable.pin2
  N3: Part3.RESET, Part3.A7
  GND: Part3.GND, Part3.D13~, R25.Pin_1, R26.Pin_1, R28.Pin_1, R29.Pin_1, R31.Pin_1, R32.Pin_1, LM1084-3_3V1.GND, C3.-, C4.-, EXT.5, R39.Pin_1, R40.Pin_1, FUEL_2.pin3, FUEL_2.pin4, OX_2.pin4, EXT_2.pin4, STEP_UP.2, STEP_UP.11, STEP_UP.12, STEP_UP.13, STEP_UP.22, STEP_DOWN.11, STEP_DOWN.12, STEP_DOWN.13, STEP_DOWN.22, C3_2.-, C3_2.+, C5.-, C5.+, C6.-, C6.+, C7.-, C7.+, C8.-, C9.-, C10.-, C11.-
  N4: Part3.D2, STEP_DOWN.9
  N5: Part3.D3~, STEP_DOWN.8
  N6: Part3.D4, STEP_DOWN.7
  N7: Part3.D5~, OX_2.pin3
  N8: Part3.D6~, STEP_DOWN.5
  N9: Part3.D9~, STEP_UP.6
  N10: Part3.D10~, STEP_UP.5
  N11: Part3.D11/MOSI, Part3.+5V
  N12: Part3.D12~/MISO, STEP_DOWN.4
  N13: Part3.VIN, LM1084-3_3V1.output_voltage, C3.+, FUEL_2.pin1, OX_2.pin1, EXT_2.pin1, STEP_UP.23, STEP_UP.24, STEP_DOWN.23, STEP_DOWN.24, C8.+, C9.+, C10.+, C11.+
  N14: Part3.A3, STEP_UP.3
  N15: Part3.A2, STEP_UP.4
  N16: Part3.A1, STEP_UP.7
  N17: Part3.A0, STEP_UP.8
  N18: LED1.cathode, R32.Pin_0
  N19: LED2.cathode, R31.Pin_0
  N20: LED3.cathode, R40.Pin_0
  N21: LED4.cathode, R29.Pin_0
  N22: LED5.cathode, R28.Pin_0
  N23: LED6.cathode, R39.Pin_0
  N24: LED7.cathode, R26.Pin_0
  N25: LED8.cathode, R25.Pin_0
  N26: LM1084-3_3V1.input_voltage, C4.+, EXT.6, STEP_UP.1, STEP_DOWN.1, STEP_DOWN.2
  N27: OX.1, OX_2.pin8
  N28: OX.2, OX_2.pin7
  N29: OX.3, OX_2.pin6
  N30: OX.4, OX_2.pin5
  N31: OX.6, FUEL.6
  N32: OX.7, STEP_UP.16
  N33: OX.8, STEP_UP.18
  N34: OX.9, STEP_UP.20
  N35: FUEL.1, FUEL_2.pin8
  N36: FUEL.2, FUEL_2.pin7
  N37: FUEL.3, FUEL_2.pin6
  N38: FUEL.4, FUEL_2.pin5
  N39: FUEL.7, STEP_UP.17
  N40: FUEL.8, STEP_UP.19
  N41: FUEL.9, STEP_UP.21
  N42: EXT.1, EXT_2.pin8
  N43: EXT.2, EXT_2.pin7
  N44: EXT.3, EXT_2.pin6
  N45: EXT.4, EXT_2.pin5
  N46: EXT.7, STEP_DOWN.15
  N47: EXT.8, STEP_DOWN.16
  N48: EXT.9, STEP_DOWN.17
  N49: FUEL_2.pin2, STEP_DOWN.20
  N50: OX_2.pin2, STEP_DOWN.19
  N51: EXT_2.pin2, STEP_DOWN.18
  N52: STEP_DOWN.6, TX_Enable.pin1

custom parts:
  Arduino Nano 33 IOT: The Arduino Nano 33 IoT is the easiest and cheapest point of entry to enhance existing devices (and creating new ones) to be part of the IoT and designing pico-network applications. Whether you are looking at building a sensor network connected to your office or home router, or if you want to create a BLE device sending data to a cellphone, the Nano 33 IoT is your one-stop-solution for many of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
