# Fritzing sketch Controller-Schematic-Rev_E (saved by Fritzing 0.9.10b)
breadboards: 3

parts:
  Part3 = Arduino Nano 33 IOT
  LM1084-3_3V1 = Voltage Regulator - 3.3V [part_number=LM1084IT-3.3/NOPB package="TO220 [THT]"]
  C2 = Tantalum Capacitor [capacitance=10µF voltage=10V package="200 mil [THT, tantalum]"]
  C1 = Electrolytic Capacitor [capacitance=10µF voltage=16V part_number=ECA-1CM100I package="100 mil [THT, electrolytic]"]
  OX = DB9 Connector [package=db9]
  FUEL = DB9 Connector [package=db9]
  FUEL_2 = IC, DIP package, 8 pins [chip_label=LTC1690]
  OX_2 = IC, DIP package, 8 pins [chip_label=LTC1690]
  EXT = IC, DIP package, 8 pins [chip_label=LTC1690]
  ISO7740 = SO16 [chip_label=ISO7740 part_number=ISO7740 package=SO]
  ISO7741 = SO16 [chip_label=ISO7740 package=SO]
  C3 = Electrolytic Capacitor [capacitance=1µF voltage=5V package="100 mil [THT, electrolytic]"]
  C4 = Electrolytic Capacitor [capacitance=1µF voltage=5V package="100 mil [THT, electrolytic]"]
  C5 = Electrolytic Capacitor [capacitance=1µF voltage=5V package="100 mil [THT, electrolytic]"]
  C6 = Electrolytic Capacitor [capacitance=1µF voltage=5V package="100 mil [THT, electrolytic]"]
  C7 = Electrolytic Capacitor [capacitance=1µF voltage=5V package="100 mil [THT, electrolytic]"]
  C8 = Electrolytic Capacitor [capacitance=1µF voltage=5V package="100 mil [THT, electrolytic]"]
  C23 = Electrolytic Capacitor [capacitance=1µF voltage=5V package="100 mil [THT, electrolytic]"]
  C24 = Electrolytic Capacitor [capacitance=1µF voltage=5V package="100 mil [THT, electrolytic]"]
  C25 = Electrolytic Capacitor [capacitance=1µF voltage=5V package="100 mil [THT, electrolytic]"]
  C26 = Electrolytic Capacitor [capacitance=1µF voltage=5V package="100 mil [THT, electrolytic]"]
  C19 = Electrolytic Capacitor [capacitance=1µF voltage=5V package="100 mil [THT, electrolytic]"]
  C21 = Electrolytic Capacitor [capacitance=1µF voltage=5V package="100 mil [THT, electrolytic]"]
  C23_2 = Electrolytic Capacitor [capacitance=1µF voltage=5V package="100 mil [THT, electrolytic]"]
  C24_2 = Electrolytic Capacitor [capacitance=1µF voltage=5V package="100 mil [THT, electrolytic]"]
  C13 = Electrolytic Capacitor [capacitance=1µF voltage=5V package="100 mil [THT, electrolytic]"]
  C14 = Electrolytic Capacitor [capacitance=1µF voltage=5V package="100 mil [THT, electrolytic]"]
  C15 = Electrolytic Capacitor [capacitance=1µF voltage=5V package="100 mil [THT, electrolytic]"]
  C16 = Electrolytic Capacitor [capacitance=1µF voltage=5V package="100 mil [THT, electrolytic]"]
  C17 = Electrolytic Capacitor [capacitance=1µF voltage=5V package="100 mil [THT, electrolytic]"]
  C18 = Electrolytic Capacitor [capacitance=1µF voltage=5V package="100 mil [THT, electrolytic]"]
  SER_EN = single row smd female pin header, 2 pins [form="♀ (female)"]
  EXT_2 = DB9 Connector [package=db9]
  74AHC597 = 74HC595 [part_number=74AHC595 package="DIP16 [THT]"]
  74AHC598 = 74HC595 [part_number=74AHC595 package="DIP16 [THT]"]
  XGURU_RED1 = LED_BARGRAPH_10 [part_number=XGURUGX10D package=led_bargaph_10]
  XGURU_GRN1 = LED_BARGRAPH_10 [part_number=XGURUGX10D package=led_bargaph_10]
  RES_ARR1 = IC, DIP package, 16 pins [chip_label=RES part_number=4116R-1-680LF]
  R3 = Resistor [tolerance=±5% power=0.25 resistance=150 package=THT]
  R4 = Resistor [tolerance=±5% power=0.25 resistance=68 package=THT]
  C11 = Electrolytic Capacitor [capacitance=1µF voltage=5V package="100 mil [THT, electrolytic]"]
  C12 = Electrolytic Capacitor [capacitance=1µF voltage=5V package="100 mil [THT, electrolytic]"]
  C9 = Electrolytic Capacitor [capacitance=1µF voltage=5V package="100 mil [THT, electrolytic]"]
  C10 = Electrolytic Capacitor [capacitance=1µF voltage=5V package="100 mil [THT, electrolytic]"]
  SN74AXC = QFN-24 [chip_label=SN74AXC package=QFN]

nets:
  N1: Part3.RX, EXT.pin3
  N2: Part3.TX, SN74AXC.5
  N3: Part3.RESET, Part3.A7, SN74AXC.6
  GND: Part3.GND, Part3.D13~, LM1084-3_3V1.GND, C2.-, C1.-, FUEL_2.pin3, FUEL_2.pin4, OX_2.pin4, EXT.pin4, C3.-, C4.-, C5.-, C6.-, C7.-, C8.-, C13.-, C14.-, C15.-, C16.-, C17.-, C18.-, SER_EN.pin2, EXT_2.5, 74AHC597.SH_CP, 74AHC597.OE, 74AHC598.SH_CP, 74AHC598.OE, RES_ARR1.pin1, RES_ARR1.pin2, RES_ARR1.pin3, RES_ARR1.pin4, RES_ARR1.pin5, RES_ARR1.pin6, RES_ARR1.pin7, RES_ARR1.pin8, R3.Pin_0, R4.Pin_0, C9.-, C10.-, SN74AXC.2, SN74AXC.11, SN74AXC.12, SN74AXC.13, SN74AXC.22
  N4: Part3.D2, SN74AXC.8
  N5: Part3.D3~, SER_EN.pin1
  N6: Part3.D4, SN74AXC.4
  N7: Part3.D5~, OX_2.pin3
  N8: Part3.D8, 74AHC598.ST_CP
  N9: Part3.D9~, ISO7741.4
  N10: Part3.D10~, ISO7740.4
  N11: Part3.D11/MOSI, Part3.+5V, 74AHC598.DS
  N12: Part3.D12~/MISO, SN74AXC.3
  N13: Part3.VIN, LM1084-3_3V1.output_voltage, C2.+, C3.+, C4.+, C5.+, C6.+, SN74AXC.1
  N14: Part3.A6, SN74AXC.7
  N15: Part3.A3, ISO7740.3
  N16: Part3.A2, ISO7741.3
  N17: Part3.A1, ISO7740.5
  N18: Part3.A0, ISO7741.5
  N19: Part3.3V3, XGURU_GRN1.B_A
  N20: LM1084-3_3V1.input_voltage, C1.+, FUEL_2.pin1, OX_2.pin1, EXT.pin1, C7.+, C8.+, C13.+, C14.+, C15.+, C16.+, C17.+, C18.+, EXT_2.6, XGURU_GRN1.A_A, SN74AXC.23, SN74AXC.24
  N21: OX.1, OX_2.pin8
  N22: OX.2, OX_2.pin7
  N23: OX.3, OX_2.pin6
  N24: OX.4, OX_2.pin5
  N25: OX.5, ISO7741.10, ISO7741.16, C25.+, C26.+
  N26: OX.6, ISO7741.9, ISO7741.15, C25.-, C26.-
  N27: OX.7, ISO7741.14
  N28: OX.8, ISO7741.13
  N29: OX.9, ISO7741.12
  N30: FUEL.1, FUEL_2.pin8
  N31: FUEL.2, FUEL_2.pin7
  N32: FUEL.3, FUEL_2.pin6
  N33: FUEL.4, FUEL_2.pin5
  N34: FUEL.5, ISO7740.10, ISO7740.16, C23.+, C24.+
  N35: FUEL.6, ISO7740.9, ISO7740.15, C23.-, C24.-
  N36: FUEL.7, ISO7740.14
  N37: FUEL.8, ISO7740.13
  N38: FUEL.9, ISO7740.12
  N39: FUEL_2.pin2, SN74AXC.21
  N40: OX_2.pin2, SN74AXC.20
  N41: EXT.pin2, SN74AXC.19
  N42: EXT.pin5, EXT_2.4
  N43: EXT.pin6, EXT_2.3
  N44: EXT.pin7, EXT_2.2
  N45: EXT.pin8, EXT_2.1
  N46: ISO7740.1, ISO7741.1, C19.+, C21.+, C23_2.+, C24_2.+, C11.+, C12.+, C9.+, C10.+
  N47: ISO7740.2, ISO7740.8, ISO7741.2, ISO7741.8, C19.-, C21.-, C23_2.-, C24_2.-, C11.-, C12.-
  N48: EXT_2.7, SN74AXC.16
  N49: EXT_2.8, SN74AXC.17
  N50: EXT_2.9, SN74AXC.18
  N51: 74AHC597.Q1, XGURU_RED1.I_A
  N52: 74AHC597.Q2, XGURU_RED1.H_A
  N53: 74AHC597.Q3, XGURU_RED1.G_A
  N54: 74AHC597.Q4, XGURU_RED1.F_A
  N55: 74AHC597.Q5, XGURU_RED1.E_A
  N56: 74AHC597.Q6, XGURU_RED1.D_A
  N57: 74AHC597.Q7, XGURU_RED1.C_A
  VCC: 74AHC597.MR, 74AHC597.VCC, 74AHC598.MR, 74AHC598.VCC
  N58: 74AHC597.DS, 74AHC598.Q7'
  N59: 74AHC597.Q0, XGURU_RED1.J_A
  N60: 74AHC598.Q1, XGURU_GRN1.I_A
  N61: 74AHC598.Q2, XGURU_GRN1.H_A
  N62: 74AHC598.Q3, XGURU_GRN1.G_A
  N63: 74AHC598.Q4, XGURU_GRN1.F_A
  N64: 74AHC598.Q5, XGURU_GRN1.E_A
  N65: 74AHC598.Q6, XGURU_GRN1.D_A
  N66: 74AHC598.Q7, XGURU_GRN1.C_A
  N67: 74AHC598.Q0, XGURU_GRN1.J_A
  N68: XGURU_RED1.J_C, XGURU_GRN1.J_C, RES_ARR1.pin16
  N69: XGURU_RED1.I_C, XGURU_GRN1.I_C, RES_ARR1.pin15
  N70: XGURU_RED1.H_C, XGURU_GRN1.H_C, RES_ARR1.pin14
  N71: XGURU_RED1.G_C, XGURU_GRN1.G_C, RES_ARR1.pin13
  N72: XGURU_RED1.F_C, XGURU_GRN1.F_C, RES_ARR1.pin12
  N73: XGURU_RED1.E_C, XGURU_GRN1.E_C, RES_ARR1.pin11
  N74: XGURU_RED1.D_C, XGURU_GRN1.D_C, RES_ARR1.pin10
  N75: XGURU_RED1.C_C, XGURU_GRN1.C_C, RES_ARR1.pin9
  N76: XGURU_GRN1.B_C, R4.Pin_1
  N77: XGURU_GRN1.A_C, R3.Pin_1

notes:
  Differences between Fritzing info and actual:
  >ISO 7740s are SOIC-16, not SO-16
  >Capacitor sizes:
  -

custom parts:
  Arduino Nano 33 IOT: The Arduino Nano 33 IoT is the easiest and cheapest point of entry to enhance existing devices (and creating new ones) to be part of the IoT and designing pico-network applications. Whether you are looking at building a sensor network connected to your office or home router, or if you want to create a BLE device sending data to a cellphone, the Nano 33 IoT is your one-stop-solution for many of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
