# Fritzing sketch Controller-Schematic (saved by Fritzing 0.9.10b)
circuit board: 9.47749cm x 5.38626cm
breadboards: 2

parts:
  EncCLK1 = MAX485 [package=dil08]
  Arduino_Nano_33_IoT = Arduino Nano 33 IOT
  EncDat1 = MAX485 [package=dil08]
  FUEL = DB15 VGA Connector [package=db15]
  OX = DB15 VGA Connector [package=db15]
  EncDat2 = MAX485 [package=dil08]
  EncCLK2 = MAX485 [package=dil08]
  R3 = Resistor [tolerance=±5% power=0.25 resistance=100 package=THT]
  R4 = Resistor [tolerance=±5% power=0.25 resistance=100 package=THT]
  R5 = Resistor [tolerance=±5% power=0.25 resistance=100 package=THT]
  R6 = Resistor [tolerance=±5% power=0.25 resistance=100 package=THT]
  R7 = Resistor [tolerance=±5% power=0.25 resistance=1k package=THT]
  R8 = Resistor [tolerance=±5% power=0.25 resistance=1k package=THT]
  Adjust-High_or_Low = Toggle Switch [package=THT]
  << = Pushbutton [package="[THT]"]
  >> = Pushbutton [package="[THT]"]
  R10 = Resistor [tolerance=±5% power=0.25 resistance=10k package=THT]
  R11 = Resistor [tolerance=±5% power=0.25 resistance=10k package=THT]
  R12 = Resistor [tolerance=±5% power=0.25 resistance=100 package=THT]
  R13 = Resistor [tolerance=±5% power=0.25 resistance=220 package=THT]
  R14 = Resistor [tolerance=±5% power=0.25 resistance=220 package=THT]
  R15 = Resistor [tolerance=±5% power=0.25 resistance=220 package=THT]
  R16 = Resistor [tolerance=±5% power=0.25 resistance=220 package=THT]
  R17 = Resistor [tolerance=±5% power=0.25 resistance=10k package=THT]
  R18 = Resistor [tolerance=±5% power=0.25 resistance=10k package=THT]

nets:
  N1: EncCLK1.RO, Arduino_Nano_33_IoT.RX
  N2: EncCLK1.RE, R3.Pin_0
  GND: EncCLK1.GND, Arduino_Nano_33_IoT.GND, Arduino_Nano_33_IoT.D13~, EncDat1.GND, FUEL.GND, OX.GND, EncDat2.GND, EncCLK2.GND, R3.Pin_1, R4.Pin_0, R10.Pin_0, R11.Pin_0, R12.Pin_0, R17.Pin_1, R18.Pin_1
  N3: EncCLK1.A, FUEL.CLK-
  N4: EncCLK1.B, FUEL.CLK+
  VCC: EncCLK1.VCC, Arduino_Nano_33_IoT.VIN, EncDat1.VCC, FUEL.5V, OX.5V, EncDat2.VCC, EncCLK2.VCC, R5.Pin_1, R6.Pin_0, Adjust-High_or_Low.L1, <<.Pin_1, <<.Pin_2, >>.Pin_1, >>.Pin_2
  N5: Arduino_Nano_33_IoT.TX, EncDat1.DI
  N6: Arduino_Nano_33_IoT.RESET, Arduino_Nano_33_IoT.A7, OX.ADJ+, R18.Pin_0
  N7: Arduino_Nano_33_IoT.D2, FUEL.ADJ-R, OX.ADJ-R, >>.Pin_3, >>.Pin_4, R11.Pin_1
  N8: Arduino_Nano_33_IoT.D3~, Adjust-High_or_Low.COM
  N9: Arduino_Nano_33_IoT.D4, R16.Pin_1
  N10: Arduino_Nano_33_IoT.D5~, R15.Pin_0
  N11: Arduino_Nano_33_IoT.D6~, R7.Pin_1
  N12: Arduino_Nano_33_IoT.D7, R8.Pin_1
  N13: Arduino_Nano_33_IoT.D8, R14.Pin_1
  N14: Arduino_Nano_33_IoT.D9~, FUEL.ADJ-L, OX.ADJ-L, <<.Pin_3, <<.Pin_4, R10.Pin_1
  N15: Arduino_Nano_33_IoT.D10~, R13.Pin_0
  N16: Arduino_Nano_33_IoT.D11/MOSI, Arduino_Nano_33_IoT.+5V, EncDat2.DI
  N17: Arduino_Nano_33_IoT.D12~/MISO, EncCLK2.RO
  N18: Arduino_Nano_33_IoT.A6, FUEL.H3
  N19: Arduino_Nano_33_IoT.A5, FUEL.H2
  N20: Arduino_Nano_33_IoT.A4, FUEL.H1
  N21: Arduino_Nano_33_IoT.A3, OX.H1
  N22: Arduino_Nano_33_IoT.A2, OX.H2
  N23: Arduino_Nano_33_IoT.A1, OX.H3
  N24: Arduino_Nano_33_IoT.A0, FUEL.ADJ+, R17.Pin_0
  N25: EncDat1.DE, R5.Pin_0
  N26: EncDat1.A, FUEL.DATA-
  N27: EncDat1.B, FUEL.DATA+
  N28: FUEL.CTRL, R13.Pin_1
  N29: FUEL.DIR, R15.Pin_1
  N30: FUEL.STOP, R7.Pin_0
  N31: OX.CLK+, EncCLK2.A
  N32: OX.CLK-, EncCLK2.B
  N33: OX.DATA+, EncDat2.A
  N34: OX.DATA-, EncDat2.B
  N35: OX.CTRL, R14.Pin_0
  N36: OX.DIR, R16.Pin_0
  N37: OX.STOP, R8.Pin_0
  N38: EncDat2.DE, R6.Pin_1
  N39: EncCLK2.RE, R4.Pin_1
  N40: Adjust-High_or_Low.L2, R12.Pin_1

notes:
  MAX485EEPA+
  L        R
  Valve. Adj.
  MEAT Valve Control Board, Rev.: -.1

custom parts:
  Arduino Nano 33 IOT: The Arduino Nano 33 IoT is the easiest and cheapest point of entry to enhance existing devices (and creating new ones) to be part of the IoT and designing pico-network applications. Whether you are looking at building a sensor network connected to your office or home router, or if you want to create a BLE device sending data to a cellphone, the Nano 33 IoT is your one-stop-solution for many of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
